// Logisim project meuRelogio.circ as structural Verilog: 5 circuits, main circuit main
module main (
  input  in_1,
  input  in_2,
  input  in_3,
  input  in_4
);

  wire bcdci_1_a, bcdci_1_b, bcdci_1_c, bcdci_1_d, bcdci_1_e, bcdci_1_f, bcdci_1_g;

  bcdCI bcdci_1 (
    .in_1({in_4, in_3, in_2, in_1}), .A(bcdci_1_a), .B(bcdci_1_b), .C(bcdci_1_c), .D(bcdci_1_d),
    .E(bcdci_1_e), .F(bcdci_1_f), .G(bcdci_1_g));
  _7_Segment_Display u_7_segment_display_1 (
    .g(bcdci_1_g), .f(bcdci_1_f), .a(bcdci_1_a), .b(bcdci_1_b), .e(bcdci_1_e), .d(bcdci_1_d), .c(bcdci_1_c));  // open: dp
endmodule

module CONTADOR_0_9 (
  input  RESET,
  input  CLK,
  output PULSE,
  output [3:0] OUT
);

  wire or_1_out;

  T_Flip_Flop #(.trigger("falling")) t_ff_1 (.clk(CLK), .T(1'b1), .Q(OUT[0]), .reset(or_1_out));  // open: Qn, preset
  T_Flip_Flop #(.trigger("falling")) t_ff_2 (.clk(OUT[0]), .T(1'b1), .Q(OUT[1]), .reset(or_1_out));  // open: Qn, preset
  and and_1 (PULSE, ~OUT[0], OUT[1], ~OUT[2], OUT[3]);  // AND_Gate
  T_Flip_Flop #(.trigger("falling")) t_ff_3 (.clk(OUT[1]), .T(1'b1), .Q(OUT[2]), .reset(or_1_out));  // open: Qn, preset
  or or_1 (or_1_out, PULSE, RESET);
  T_Flip_Flop #(.trigger("falling")) t_ff_4 (.clk(OUT[2]), .T(1'b1), .Q(OUT[3]), .reset(or_1_out));  // open: Qn, preset
endmodule

module bcdCI (
  input  [3:0] in_1,
  output A,
  output B,
  output C,
  output D,
  output E,
  output F,
  output G
);

  Multiplexer #(.select(4), .enable("false")) multiplexer_1 (
    .in0(1'b1), .in1(1'b0), .in2(1'b1), .in3(1'b1), .in4(1'b0), .in5(1'b1), .in6(1'b1), .in7(1'b1),
    .in8(1'b1), .in9(1'b1), .in10(1'b0), .in11(1'b0), .in12(1'b0), .in13(1'b0), .in14(1'b0), .in15(1'b0),
    .out(A), .sel(in_1));
  Multiplexer #(.select(4), .enable("false")) multiplexer_2 (
    .in0(1'b1), .in1(1'b1), .in2(1'b1), .in3(1'b1), .in4(1'b1), .in5(1'b0), .in6(1'b0), .in7(1'b1),
    .in8(1'b1), .in9(1'b1), .in10(1'b0), .in11(1'b0), .in12(1'b0), .in13(1'b0), .in14(1'b0), .in15(1'b0),
    .out(B), .sel(in_1));
  Multiplexer #(.select(4), .enable("false")) multiplexer_3 (
    .in0(1'b1), .in1(1'b1), .in2(1'b0), .in3(1'b1), .in4(1'b1), .in5(1'b1), .in6(1'b1), .in7(1'b1),
    .in8(1'b1), .in9(1'b1), .in10(1'b0), .in11(1'b0), .in12(1'b0), .in13(1'b0), .in14(1'b0), .in15(1'b0),
    .out(C), .sel(in_1));
  Multiplexer #(.select(4), .enable("false")) multiplexer_4 (
    .in0(1'b1), .in1(1'b0), .in2(1'b1), .in3(1'b1), .in4(1'b0), .in5(1'b1), .in6(1'b1), .in7(1'b0),
    .in8(1'b1), .in9(1'b0), .in10(1'b0), .in11(1'b0), .in12(1'b0), .in13(1'b0), .in14(1'b0), .in15(1'b0),
    .out(D), .sel(in_1));
  Multiplexer #(.select(4), .enable("false")) multiplexer_5 (
    .in0(1'b1), .in1(1'b0), .in2(1'b1), .in3(1'b0), .in4(1'b0), .in5(1'b0), .in6(1'b1), .in7(1'b0),
    .in8(1'b1), .in9(1'b0), .in10(1'b0), .in11(1'b0), .in12(1'b0), .in13(1'b0), .in14(1'b0), .in15(1'b0),
    .out(E), .sel(in_1));
  Multiplexer #(.select(4), .enable("false")) multiplexer_6 (
    .in0(1'b1), .in1(1'b0), .in2(1'b0), .in3(1'b0), .in4(1'b1), .in5(1'b1), .in6(1'b1), .in7(1'b0),
    .in8(1'b1), .in9(1'b1), .in10(1'b0), .in11(1'b0), .in12(1'b0), .in13(1'b0), .in14(1'b0), .in15(1'b0),
    .out(F), .sel(in_1));
  Multiplexer #(.select(4), .enable("false")) multiplexer_7 (
    .in0(1'b0), .in1(1'b0), .in2(1'b1), .in3(1'b1), .in4(1'b1), .in5(1'b1), .in6(1'b1), .in7(1'b0),
    .in8(1'b1), .in9(1'b1), .in10(1'b0), .in11(1'b0), .in12(1'b0), .in13(1'b0), .in14(1'b0), .in15(1'b0),
    .out(G), .sel(in_1));
endmodule

module CONTADOR_0_5 (
  input  RESET,
  input  CLK,
  output PULSE,
  output [3:0] OUT
);

  wire or_1_out;

  T_Flip_Flop #(.trigger("falling")) t_ff_1 (.clk(CLK), .T(1'b1), .Q(OUT[0]), .reset(or_1_out));  // open: Qn, preset
  T_Flip_Flop #(.trigger("falling")) t_ff_2 (.clk(OUT[0]), .T(1'b1), .Q(OUT[1]), .reset(or_1_out));  // open: Qn, preset
  and and_1 (PULSE, ~OUT[0], OUT[1], OUT[2]);  // AND_Gate
  T_Flip_Flop #(.trigger("falling")) t_ff_3 (.clk(OUT[1]), .T(1'b1), .Q(OUT[2]), .reset(or_1_out));  // open: Qn, preset
  or or_1 (or_1_out, PULSE, RESET);

  assign OUT[3] = 1'b0;
endmodule

module RELOGIO (
);

  wire and_1_out, and_2_out, and_3_out, bcdci_1_a, bcdci_1_b, bcdci_1_c, bcdci_1_d, bcdci_1_e, bcdci_1_f,
       bcdci_1_g, bcdci_2_a, bcdci_2_b, bcdci_2_c, bcdci_2_d, bcdci_2_e, bcdci_2_f, bcdci_2_g, bcdci_3_a,
       bcdci_3_b, bcdci_3_c, bcdci_3_d, bcdci_3_e, bcdci_3_f, bcdci_3_g, bcdci_4_a, bcdci_4_b, bcdci_4_c,
       bcdci_4_d, bcdci_4_e, bcdci_4_f, bcdci_4_g, bcdci_5_a, bcdci_5_b, bcdci_5_c, bcdci_5_d, bcdci_5_e,
       bcdci_5_f, bcdci_5_g, bcdci_6_a, bcdci_6_b, bcdci_6_c, bcdci_6_d, bcdci_6_e, bcdci_6_f, bcdci_6_g,
       clock_1_out, contador_0_5_2_pulse, contador_0_5_3_pulse, contador_0_9_1_pulse, contador_0_9_2_pulse,
       contador_0_9_3_pulse;
  wire [3:0] contador_0_5_1_out, contador_0_5_2_out, contador_0_5_3_out, contador_0_9_1_out,
       contador_0_9_2_out, contador_0_9_3_out;

  and and_1 (and_1_out, ~contador_0_5_1_out[0], contador_0_5_1_out[1], ~contador_0_5_1_out[2], ~contador_0_5_1_out[3]);  // AND_Gate
  and and_2 (and_2_out, and_1_out, and_3_out);
  and and_3 (and_3_out, ~contador_0_9_1_out[0], ~contador_0_9_1_out[1], contador_0_9_1_out[2], ~contador_0_9_1_out[3]);  // AND_Gate
  bcdCI bcdci_1 (
    .in_1(contador_0_5_1_out), .A(bcdci_1_a), .B(bcdci_1_b), .C(bcdci_1_c), .D(bcdci_1_d), .E(bcdci_1_e),
    .F(bcdci_1_f), .G(bcdci_1_g));
  _7_Segment_Display u_7_segment_display_1 (
    .g(bcdci_1_g), .f(bcdci_1_f), .a(bcdci_1_a), .b(bcdci_1_b), .e(bcdci_1_e), .d(bcdci_1_d), .c(bcdci_1_c));  // open: dp
  _7_Segment_Display u_7_segment_display_2 (
    .g(bcdci_3_g), .f(bcdci_3_f), .a(bcdci_3_a), .b(bcdci_3_b), .e(bcdci_3_e), .d(bcdci_3_d), .c(bcdci_3_c));  // open: dp
  CONTADOR_0_5 contador_0_5_1 (.RESET(and_2_out), .OUT(contador_0_5_1_out), .CLK(contador_0_9_1_pulse));  // open: PULSE
  bcdCI bcdci_2 (
    .in_1(contador_0_5_2_out), .A(bcdci_2_a), .B(bcdci_2_b), .C(bcdci_2_c), .D(bcdci_2_d), .E(bcdci_2_e),
    .F(bcdci_2_f), .G(bcdci_2_g));
  bcdCI bcdci_3 (
    .in_1(contador_0_9_1_out), .A(bcdci_3_a), .B(bcdci_3_b), .C(bcdci_3_c), .D(bcdci_3_d), .E(bcdci_3_e),
    .F(bcdci_3_f), .G(bcdci_3_g));
  _7_Segment_Display u_7_segment_display_3 (
    .g(bcdci_2_g), .f(bcdci_2_f), .a(bcdci_2_a), .b(bcdci_2_b), .e(bcdci_2_e), .d(bcdci_2_d), .c(bcdci_2_c));  // open: dp
  CONTADOR_0_9 contador_0_9_1 (
    .PULSE(contador_0_9_1_pulse), .RESET(and_2_out), .OUT(contador_0_9_1_out), .CLK(contador_0_5_2_pulse));
  CONTADOR_0_5 contador_0_5_2 (
    .PULSE(contador_0_5_2_pulse), .OUT(contador_0_5_2_out), .CLK(contador_0_9_2_pulse));  // open: RESET
  bcdCI bcdci_4 (
    .in_1(contador_0_9_2_out), .A(bcdci_4_a), .B(bcdci_4_b), .C(bcdci_4_c), .D(bcdci_4_d), .E(bcdci_4_e),
    .F(bcdci_4_f), .G(bcdci_4_g));
  _7_Segment_Display u_7_segment_display_4 (
    .g(bcdci_4_g), .f(bcdci_4_f), .a(bcdci_4_a), .b(bcdci_4_b), .e(bcdci_4_e), .d(bcdci_4_d), .c(bcdci_4_c));  // open: dp
  CONTADOR_0_9 contador_0_9_2 (
    .PULSE(contador_0_9_2_pulse), .OUT(contador_0_9_2_out), .CLK(contador_0_5_3_pulse));  // open: RESET
  bcdCI bcdci_5 (
    .in_1(contador_0_5_3_out), .A(bcdci_5_a), .B(bcdci_5_b), .C(bcdci_5_c), .D(bcdci_5_d), .E(bcdci_5_e),
    .F(bcdci_5_f), .G(bcdci_5_g));
  _7_Segment_Display u_7_segment_display_5 (
    .g(bcdci_6_g), .f(bcdci_6_f), .a(bcdci_6_a), .b(bcdci_6_b), .e(bcdci_6_e), .d(bcdci_6_d), .c(bcdci_6_c));  // open: dp
  _7_Segment_Display u_7_segment_display_6 (
    .g(bcdci_5_g), .f(bcdci_5_f), .a(bcdci_5_a), .b(bcdci_5_b), .e(bcdci_5_e), .d(bcdci_5_d), .c(bcdci_5_c));  // open: dp
  CONTADOR_0_5 contador_0_5_3 (
    .PULSE(contador_0_5_3_pulse), .OUT(contador_0_5_3_out), .CLK(contador_0_9_3_pulse));  // open: RESET
  Clock clock_1 (.out(clock_1_out));
  bcdCI bcdci_6 (
    .in_1(contador_0_9_3_out), .A(bcdci_6_a), .B(bcdci_6_b), .C(bcdci_6_c), .D(bcdci_6_d), .E(bcdci_6_e),
    .F(bcdci_6_f), .G(bcdci_6_g));
  CONTADOR_0_9 contador_0_9_3 (
    .PULSE(contador_0_9_3_pulse), .OUT(contador_0_9_3_out), .CLK(clock_1_out));  // open: RESET
endmodule
